# Fritzing sketch Fritzing (saved by Fritzing 0.9.3b)
breadboards: 1

parts:
  U1 = Adafruit ATWINC1500 WiFi Breakout [package="SIP (Single Inline) [THT]"]
  Part1 = Arduino Uno (Rev3)

nets:
  VIN: U1.Vin, U1.EN, Part1.5V
  GND: U1.GND, Part1.GND
  N1: U1.SCK, Part1.D13/SCK
  N2: U1.MISO, Part1.D12/MISO
  N3: U1.MOSI, Part1.D11_PWM/MOSI
  N4: U1.CS, Part1.D8
  N5: U1.IRQ, Part1.D7
  N6: U1.RST, Part1.D4

custom parts:
  Adafruit ATWINC1500 WiFi Breakout: https://www.adafruit.com/product/2999
